# Fritzing sketch AnalogInput (saved by Fritzing 0.9.3b)
breadboards: 1

parts:
  U1 = POT [package=pot_alpha_rv16af-20]
  U2 = POT [package=pot_alpha_rv16af-20]
  U3 = POT [package=pot_alpha_rv16af-20]
  IC1 = MCP3008 8-channel 10-bit ADC [part_number=MCP3008]
  Part1 = 12 NeoPixel Ring [part_number=1643]
  Raspberry_Pi_1 = Raspberry Pi 3 [part_number=RPI-3-V1.2]

nets:
  GND: U1.A, U2.A, U3.A, IC1.no_name_yet#9, IC1.no_name_yet#14, Part1.GND, Raspberry_Pi_1.GND
  N1: U1.S, IC1.no_name_yet#1
  VDD: U1.E, U2.E, U3.E, IC1.no_name_yet#15, IC1.no_name_yet#16, Part1.VDD, Raspberry_Pi_1.3v3
  N2: U2.S, IC1.no_name_yet#2
  N3: U3.S, IC1.no_name_yet#3
  N4: IC1.no_name_yet#10, Raspberry_Pi_1.GIPO8
  N5: IC1.no_name_yet#11, Raspberry_Pi_1.GIPO10
  N6: IC1.no_name_yet#12, Raspberry_Pi_1.GIPO9
  N7: IC1.no_name_yet#13, Raspberry_Pi_1.GIPO11
  N8: Part1.IN, Raspberry_Pi_1.GIPO18

custom parts:
  12 NeoPixel Ring: 12 ultra bright smart LED NeoPixels are arranged in a circle with 1.5" (37mm) outer diameter. The rings are 'chainable' - connect the output pin of one to the input pin of another. Use only one microcontroller pin to control as many as you can chain together! Each LED is addressable as the driver chip is inside the LED. Each one has ~18mA constant current drive so the color will be very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
